# Fritzing sketch expérience 1 (saved by Fritzing 0.9.3b)
breadboards: 1

parts:
  L1 = Inductor [package="400 mil [THT]"]
  R1 = Resistor [tolerance=±5% resistance=100 package=THT]
  Composant1 = Arduino Uno (Rev3)
  R2 = Resistor [tolerance=±5% resistance=100k package=THT]

nets:
  electrode: L1.pin_0, Composant1.A0, R2.Pin_1
  N1: L1.pin_1, R1.Pin_0
  N2: R1.Pin_1, Composant1.D9_PWM
  GND: Composant1.GND, R2.Pin_0
